# Fritzing sketch 7segment (saved by Fritzing 0.9.3b)

parts:
  Part1 = Arduino Pro Mini v13
  ZS-042_RTC1 = ZS-042 RTC Module
  S1 = Pushbutton [package="[THT]"]
  R1 = Resistor [tolerance=±5% resistance=470 package=THT]
  S2 = Pushbutton [package="[THT]"]
  S3 = Pushbutton [package="[THT]"]
  R2 = Resistor [tolerance=±5% resistance=470 package=THT]
  U1 = Mini-360 DC-DC Buck converter [package=THT]
  Q1 = NPN-Transistor [part_number=BC547 package="TO92 [THT]"]
  Q2 = NPN-Transistor [part_number=BC547 package="TO92 [THT]"]
  Q3 = NPN-Transistor [part_number=BC547 package="TO92 [THT]"]
  Q4 = NPN-Transistor [part_number=BC547 package="TO92 [THT]"]
  D1 = Rectifier Diode [part_number=1N5408 package="300 mil [THT]"]
  R3 = Resistor [tolerance=±5% resistance=470 package=THT]
  7_Segment1 = 7 Segment Display
  7_Segment2 = 7 Segment Display
  7_Segment3 = 7 Segment Display
  7_Segment4 = 7 Segment Display
  LED1 = LED - 5mm [color="Red (633nm)" package="5 mm [THT]"]
  LED2 = LED - 5mm [color="Red (633nm)" package="5 mm [THT]"]
  R4 = Resistor [tolerance=±5% resistance=470 package=THT]

nets:
  5V: Part1.VCC, Part1.RAW, ZS-042_RTC1.VCC, R1.Pin_0, R2.Pin_0, U1.OUT+, R3.Pin_0, R4.Pin_1
  N1: Part1.A4, ZS-042_RTC1.SDA
  N2: Part1.A5, ZS-042_RTC1.SCL
  GND: Part1.GND, ZS-042_RTC1.GND, S1.Pin_3, S1.Pin_4, S2.Pin_3, S2.Pin_4, S3.Pin_3, S3.Pin_4, U1.IN-, U1.OUT-, Q1.E, Q2.E, Q3.E, Q4.E
  N3: Part1.A3, Q1.B
  N4: Part1.A2, Q2.B
  N5: Part1.A1, Q3.B
  N6: Part1.A0, Q4.B
  N7: Part1.D13/SCK, LED1.cathode, LED2.cathode
  N8: Part1.D12/MISO, R1.Pin_1, S3.Pin_1, S3.Pin_2
  N9: Part1.D11_PWM/MOSI, S2.Pin_1, S2.Pin_2, R2.Pin_1
  N10: Part1.D10_PWM/SS, S1.Pin_1, S1.Pin_2, R3.Pin_1
  N11: Part1.D8, 7_Segment1.Segment_C, 7_Segment2.Segment_C, 7_Segment3.Segment_C, 7_Segment4.Segment_C
  N12: Part1.D7, 7_Segment1.Segment_G, 7_Segment2.Segment_G, 7_Segment3.Segment_G, 7_Segment4.Segment_G
  N13: Part1.D6_PWM, 7_Segment1.Segment_F, 7_Segment2.Segment_F, 7_Segment3.Segment_F, 7_Segment4.Segment_F
  N14: Part1.D5_PWM, 7_Segment1.Segment_A, 7_Segment2.Segment_A, 7_Segment3.Segment_A, 7_Segment4.Segment_A
  N15: Part1.D4, 7_Segment1.Segment_B, 7_Segment2.Segment_B, 7_Segment3.Segment_B, 7_Segment4.Segment_B
  N16: Part1.D3_PWM, 7_Segment1.Segment_D, 7_Segment2.Segment_D, 7_Segment3.Segment_D, 7_Segment4.Segment_D
  N17: Part1.D2, 7_Segment1.Segment_E, 7_Segment2.Segment_E, 7_Segment3.Segment_E, 7_Segment4.Segment_E
  N18: U1.IN+, D1.cathode
  N19: Q1.C, 7_Segment1.common_cathode
  N20: Q2.C, 7_Segment2.common_cathode
  N21: Q3.C, 7_Segment3.common_cathode
  N22: Q4.C, 7_Segment4.common_cathode
  12V: D1.anode
  N23: LED1.anode, LED2.anode, R4.Pin_0

notes:
  F
  A
  B
  C
  D
  E
  G

custom parts:
  Mini-360 DC-DC Buck converter: Mini-360 DC-DC Buck converter. Tiny buck step down voltage converter, input voltage 4.75 to 23V output 1 to 17V adjustable. Available from ebay and the like.
